// Logisim project processor_riscv_evolution.circ as structural Verilog
module ALU (
  input  [2:0] F,
  input  [31:0] B,
  input  [31:0] A,
  output Zero_flag,
  output [31:0] Y,
  output Negative,
  output Carry_Out,
  output Overflow
);

  wire adder_1_cout, comparator_1_eq, comparator_1_gt, comparator_1_lt, not_2_out, xnor_1_out, xor_1_out;
  wire [31:0] adder_1_out, and_1_out, bit_extender_1_out, multiplexer_1_out, not_1_out, or_1_out;

  assign not_1_out = ~B;  // NOT_Gate not_1, 32 bits wide
  Multiplexer #(.width(32)) multiplexer_1 (.in0(B), .in1(not_1_out), .out(multiplexer_1_out), .sel(F[0]));
  Adder #(.width(32)) adder_1 (.a(multiplexer_1_out), .b(A), .out(adder_1_out), .cin(F[0]), .cout(adder_1_cout));
  assign and_1_out = A & B;  // AND_Gate and_1, 32 bits wide
  assign or_1_out = A | B;  // OR_Gate or_1, 32 bits wide
  Comparator #(.width(32)) comparator_1 (
    .a(B), .b(A), .gt(comparator_1_gt), .eq(comparator_1_eq), .lt(comparator_1_lt));
  xor xor_1 (xor_1_out, adder_1_out[31], A[31]);
  NotExactlyOne xnor_1 (.out(xnor_1_out), .in0(A[31]), .in1(B[31]), .in2(F[0]));
  assign bit_extender_1_out = {{31{comparator_1_gt}}, comparator_1_gt};  // Bit_Extender bit_extender_1
  not not_2 (not_2_out, F[1]);
  and and_2 (Carry_Out, adder_1_cout, not_2_out);
  and and_3 (Overflow, not_2_out, xor_1_out, xnor_1_out);
  Multiplexer #(.select(3), .width(32)) multiplexer_2 (
    .in0(adder_1_out), .in1(adder_1_out), .in2(and_1_out), .in3(or_1_out), .in5(bit_extender_1_out),
    .out({Negative, Y[30:0]}));  // open: in4, in6, in7, sel
  Comparator #(.mode("unsigned"), .width(32)) comparator_2 (
    .a({32{1'b0}}), .b({Negative, Y[30:0]}), .eq(Zero_flag));  // open: gt, lt

  assign Y[31] = Negative;

  // Notes on the sheet:
  //   A: initial=0xffffffff
  //   F: initial=0x5
  //   A_31
  //   B_31
  //   ALIControl_1
  //   ALUControl_0
  //   SUM_31
  //   ALUControl_2:0
endmodule

module Datapath (
  output [31:0] t2,
  output [31:0] out_2
);

  wire alu_1_zero_flag, and_1_out, CLK_out, Control_Unit_alusrc, Control_Unit_branch, Control_Unit_regwrite,
       RST_out;
  wire [2:0] Control_Unit_alucontrol;
  wire [7:0] adder_1_out, adder_2_out, bitselector_1_out, multiplexer_1_out, PC_Register_q, shifter_1_out;
  wire [31:0] alu_1_y, bit_extender_1_out, multiplexer_2_out, Register_File_rd1, Register_File_rd2;

  Multiplexer #(.width(8)) multiplexer_1 (
    .in0(adder_1_out), .in1(adder_2_out), .out(multiplexer_1_out), .sel(and_1_out));
  Clock CLK (.out(CLK_out));
  Register PC_Register (.D(multiplexer_1_out), .en(1'b1), .clk(CLK_out), .Q(PC_Register_q), .clr(RST_out));
  Button RST (.out(RST_out));
  Shifter #(.shift("lr")) shifter_1 (.in(PC_Register_q), .\dist (3'b010), .out(shifter_1_out));
  Adder adder_1 (.a(PC_Register_q), .b(8'h4), .out(adder_1_out));  // open: cin, cout
  ROM #(.dataWidth(32)) rom_1 (.addr(shifter_1_out), .data(t2));
  RegisterFile Register_File (
    .A3(t2[9:7]), .WE3(Control_Unit_regwrite), .WD3(alu_1_y), .CLK(CLK_out), .A1(t2[17:15]), .A2(t2[22:20]),
    .RD1(Register_File_rd1), .RD2(Register_File_rd2), .T2(out_2));
  assign bit_extender_1_out = {{20{t2[31]}}, t2[31:20]};  // Bit_Extender bit_extender_1
  Multiplexer #(.width(32)) multiplexer_2 (
    .in0(Register_File_rd2), .in1(bit_extender_1_out), .out(multiplexer_2_out), .sel(Control_Unit_alusrc));
  BitSelector #(.group(8), .width(13)) bitselector_1 (
    .in({t2[31], t2[7], t2[30:25], t2[11:8], 1'b0}), .out(bitselector_1_out), .sel(1'b0));
  ControlUnit Control_Unit (
    .Instruction(t2), .ALUControl(Control_Unit_alucontrol), .Branch(Control_Unit_branch),
    .ALUSrc(Control_Unit_alusrc), .RegWrite(Control_Unit_regwrite));
  and and_1 (and_1_out, Control_Unit_branch, alu_1_zero_flag);
  ALU alu_1 (
    .B(Register_File_rd1), .A(multiplexer_2_out), .F(Control_Unit_alucontrol), .Y(alu_1_y),
    .Zero_flag(alu_1_zero_flag));  // open: Carry_Out, Overflow, Negative
  Adder adder_2 (.a(bitselector_1_out), .b(PC_Register_q), .out(adder_2_out));  // open: cin, cout

  // Notes on the sheet:
  //   Shift by 2
  //   PC+4
  //   contents of rom_1 (hex, n*v repeats v):
  //   800293 100393 100313 2028a63 2628863 93 28333 30863 7080b3 fff30313 fe000ae3 83b3 fff28293 100313
  //   628463 fc000ce3 63
  //   BTA
endmodule

module RegisterFile (
  input  CLK,
  input  [2:0] A1,
  input  [2:0] A2,
  input  [31:0] WD3,
  input  WE3,
  input  [2:0] A3,
  output [31:0] RD1,
  output [31:0] RD2,
  output [31:0] T2
);

  wire and_1_out, and_2_out, and_3_out, and_4_out, and_5_out, and_6_out, and_7_out, comparator_1_eq,
       comparator_2_eq, decoder_1_out0, decoder_1_out1, decoder_1_out2, decoder_1_out3, decoder_1_out4,
       decoder_1_out5, decoder_1_out6, decoder_1_out7;
  wire [31:0] multiplexer_1_out, multiplexer_2_out, register_1_q, register_2_q, register_3_q, register_4_q,
       register_5_q, register_6_q, register_7_q;

  Decoder #(.select(3)) decoder_1 (
    .out0(decoder_1_out0), .out1(decoder_1_out1), .out2(decoder_1_out2), .out3(decoder_1_out3),
    .out4(decoder_1_out4), .out5(decoder_1_out5), .out6(decoder_1_out6), .out7(decoder_1_out7), .sel(A3));  // open: en
  and and_1 (and_1_out, WE3, decoder_1_out1);
  and and_2 (and_2_out, WE3, decoder_1_out2);
  and and_3 (and_3_out, WE3, decoder_1_out3);
  and and_4 (and_4_out, WE3, decoder_1_out4);
  and and_5 (and_5_out, WE3, decoder_1_out5);
  and and_6 (and_6_out, WE3, decoder_1_out6);
  and and_7 (and_7_out, WE3, decoder_1_out7);
  Register #(.width(32)) register_1 (.D({32{1'b0}}), .en(decoder_1_out0), .clk(CLK), .Q(register_1_q));  // open: clr
  Register #(.width(32)) register_2 (.D(WD3), .en(and_1_out), .clk(CLK), .Q(register_2_q));  // open: clr
  Register #(.width(32)) register_3 (.D(WD3), .en(and_2_out), .clk(CLK), .Q(register_3_q));  // open: clr
  Register #(.width(32)) register_4 (.D(WD3), .en(and_3_out), .clk(CLK), .Q(register_4_q));  // open: clr
  Register #(.width(32)) register_5 (.D(WD3), .en(and_4_out), .clk(CLK), .Q(register_5_q));  // open: clr
  Register #(.width(32)) register_6 (.D(WD3), .en(and_5_out), .clk(CLK), .Q(register_6_q));  // open: clr
  Register #(.width(32)) register_7 (.D(WD3), .en(and_6_out), .clk(CLK), .Q(register_7_q));  // open: clr
  Register #(.width(32)) register_8 (.D(WD3), .en(and_7_out), .clk(CLK), .Q(T2));  // open: clr
  Multiplexer #(.enable("true"), .select(3), .width(32)) multiplexer_1 (
    .in0(register_1_q), .in1(register_2_q), .in2(register_3_q), .in3(register_4_q), .in4(register_5_q),
    .in5(register_6_q), .in6(register_7_q), .in7(T2), .out(multiplexer_1_out), .sel(A1));  // open: en
  Multiplexer #(.enable("true"), .select(3), .width(32)) multiplexer_2 (
    .in0(register_1_q), .in1(register_2_q), .in2(register_3_q), .in3(register_4_q), .in4(register_5_q),
    .in5(register_6_q), .in6(register_7_q), .in7(T2), .out(multiplexer_2_out), .sel(A2));  // open: en
  Comparator #(.mode("unsigned"), .width(3)) comparator_1 (.a(A1), .b(3'b000), .eq(comparator_1_eq));  // open: gt, lt
  Comparator #(.mode("unsigned"), .width(3)) comparator_2 (.a(A2), .b(3'b000), .eq(comparator_2_eq));  // open: gt, lt
  Multiplexer #(.width(32)) multiplexer_3 (.in0(multiplexer_1_out), .in1({32{1'b0}}), .out(RD1), .sel(comparator_1_eq));
  Multiplexer #(.width(32)) multiplexer_4 (.in0(multiplexer_2_out), .in1({32{1'b0}}), .out(RD2), .sel(comparator_2_eq));

  // Notes on the sheet:
  //   A3: initial=0x7
  //   WE3: initial=0x1
  //   WD3: initial=0x12345678
  //   A2: initial=0x7
endmodule

module ControlUnit (
  input  [31:0] Instruction,
  output [2:0] ALUControl,
  output Branch,
  output ALUSrc,
  output RegWrite
);

  wire comparator_3_eq;

  Comparator #(.mode("unsigned"), .width(7)) comparator_1 (
    .a(Instruction[6:0]), .b(7'b1100011), .eq(Branch));  // open: gt, lt
  Comparator #(.mode("unsigned"), .width(7)) comparator_2 (
    .a(Instruction[6:0]), .b(7'b0010011), .eq(ALUSrc));  // open: gt, lt
  Comparator #(.mode("unsigned"), .width(7)) comparator_3 (
    .a(Instruction[6:0]), .b(7'b0110011), .eq(comparator_3_eq));  // open: gt, lt
  Multiplexer #(.width(3)) multiplexer_1 (.in0(3'b000), .in1(3'b001), .out(ALUControl), .sel(Branch));
  or or_1 (RegWrite, ALUSrc, comparator_3_eq);

  // Notes on the sheet:
  //   Instruction: initial=0x63
  //   OpCode
  //   beq
  //   addi
  //   add
endmodule

module Tests (
  output [31:0] Y,
  output [3:0] out_2,
  output [7:0] out_3
);


  assign out_2 = 4'b0010;
  assign out_3 = 8'h22;
  assign Y = 32'hf4010207;

  // Notes on the sheet:
  //   binary values in Logisim. Convince yourself how the bits are displayed.
  //   Example 1: A simple example that illustrates how 32-bit values are displayed as 
  //   Example 2) An example of how to extra certain bits from a (in this case) 32-bit wire. Here we extract the bits 8..11 from the 32-bit wire.
  //   Example 3) Sometimes it is useful to extra bits from different position and the re-assemble them. In this case, we extract bits 8..11 and bits 15..18 and assemble them into an 8-bit wire.
endmodule
